# Fritzing sketch Conexion-bperistalticas (saved by Fritzing 0.9.10b)
breadboards: 1

parts:
  Q1 = TIP120 Hi-Current Darlington Transistor
  Q2 = TIP120 Hi-Current Darlington Transistor
  Q3 = TIP120 Hi-Current Darlington Transistor
  Q4 = TIP120 Hi-Current Darlington Transistor
  M1 = DC Motor [voltage_(max)=6V voltage_(min)=3V]
  M2 = DC Motor [voltage_(max)=6V voltage_(min)=3V]
  M3 = DC Motor [voltage_(max)=12V voltage_(min)=5V]
  M4 = DC Motor [voltage_(max)=6V voltage_(min)=3V]
  D2 = Rectifier Diode [part_number=1N4001 package="300 mil [THT]"]
  D3 = Rectifier Diode [part_number=1N4001 package="300 mil [THT]"]
  D4 = Rectifier Diode [part_number=1N4001 package="300 mil [THT]"]
  U1 = ESP32-38PinWide [part_number=ESP32-38PinWide]
  D1 = Rectifier Diode [part_number=1N4001 package="300 mil [THT]"]
  R1 = Resistor [tolerance=±5% power=0.25 resistance=2.2k package=THT]
  R2 = Resistor [tolerance=±5% power=0.25 resistance=2.20k package=THT]
  R3 = Resistor [tolerance=±5% power=0.25 resistance=2.2k package=THT]
  R4 = Resistor [tolerance=±5% power=0.25 resistance=2.2k package=THT]
  Power_plug1 = Power plug

nets:
  N1: Q1.BASE, R2.Pin_0
  N2: Q1.COLLECTOR, M1.pin_2, D4.anode
  GND: Q1.EMITTER, Q2.EMITTER, Q3.EMITTER, Q4.EMITTER, U1.GND, Power_plug1.GND
  N3: Q2.COLLECTOR, M2.pin_2, D3.anode
  N4: Q3.BASE, R4.Pin_0
  N5: Q3.COLLECTOR, M3.pin_2, D2.anode
  N6: Q4.BASE, R1.Pin_0
  N7: Q4.COLLECTOR, M4.pin_2, D1.anode
  N8: M1.pin_1, M2.pin_1, M3.pin_1, M4.pin_1, D2.cathode, D3.cathode, D4.cathode, D1.cathode, Power_plug1.VCC
  N9: U1.GPIO17, R2.Pin_1
  N10: U1.GPIO5, R3.Pin_1
  N11: U1.GPIO18, R4.Pin_1
  N12: U1.GPIO19, R1.Pin_1

custom parts:
  ESP32-38PinWide: Generic 38-Pin ESP32 with wide format (only access to one side of pins on a breadboard) based on Stephen Lilley's HiLetgo ESP-WROOM-32 ESP32 ESP-32S Development Board.
