# Fritzing sketch Untitled Sketch (saved by Fritzing 0.9.3b)
breadboards: 1

parts:
  A1 = yf-s401 flow sensor [package=THT]
  YF-S201_Flow_Meter1 = YF-S201 Water Flow Meter
  U1 = ESP32-38PinWide [part_number=ESP32-38PinWide]
  A2 = yf-s401 flow sensor [package=THT]
  A3 = yf-s401 flow sensor [package=THT]
  A4 = yf-s401 flow sensor [package=THT]
  J1 = Basic Servo
  J2 = Basic Servo
  J3 = Basic Servo
  J4 = Basic Servo
  Power_plug1 = Power plug
  YF-S201_Flow_Meter2 = YF-S201 Water Flow Meter
  YF-S201_Flow_Meter3 = YF-S201 Water Flow Meter
  YF-S201_Flow_Meter4 = YF-S201 Water Flow Meter
  Componente1 = 16-Channel 12-bit PWM Servo Driver - I2C [part_number=815]

nets:
  VCC: A1.pin1, YF-S201_Flow_Meter1.VCC, A2.pin1, A3.pin1, A4.pin1, Power_plug1.VCC, YF-S201_Flow_Meter2.VCC, YF-S201_Flow_Meter3.VCC, YF-S201_Flow_Meter4.VCC, Componente1.PWRIN
  GND: A1.pin2, YF-S201_Flow_Meter1.GND, U1.GND, A2.pin2, A3.pin2, A4.pin2, J1.gnd, J2.gnd, J3.gnd, J4.gnd, Power_plug1.GND, YF-S201_Flow_Meter2.GND, YF-S201_Flow_Meter3.GND, YF-S201_Flow_Meter4.GND, Componente1.GND, Componente1.OE
  N1: A1.pin3, U1.GPIO32
  N2: YF-S201_Flow_Meter1.SIG, U1.GPIO27
  N3: U1.GPIO33, A3.pin3
  N4: U1.GPIO25, A2.pin3
  N5: U1.GPIO26, A4.pin3
  N6: U1.GPIO14, YF-S201_Flow_Meter2.SIG
  N7: U1.GPIO12, YF-S201_Flow_Meter3.SIG
  N8: U1.GPIO13, YF-S201_Flow_Meter4.SIG
  VIN: U1.GPIO11, U1.VIN, Componente1.VCC
  N9: U1.GPIO21, Componente1.SDA
  N10: U1.GPIO22, Componente1.SCL
  VCC_2: J1.vcc, J2.vcc, J3.vcc, J4.vcc, Componente1.5.0V
  N11: J1.pulse, Componente1.PWM15
  N12: J2.pulse, Componente1.PWM11
  N13: J3.pulse, Componente1.PWM7
  N14: J4.pulse, Componente1.PWM3

custom parts:
  yf-s401 flow sensor: Flow sensors sit in line with your water line, and uses a pinwheel sensor to measure how much liquid has moved through it.
  YF-S201 Water Flow Meter: The YF-S201 Flow Meter. The input voltage is 5V to 24V (DC).
  ESP32-38PinWide: Generic 38-Pin ESP32 with wide format (only access to one side of pins on a breadboard) based on Stephen Lilley's HiLetgo ESP-WROOM-32 ESP32 ESP-32S Development Board.
  16-Channel 12-bit PWM Servo Driver - I2C: You want to make a cool robot, maybe a hexapod walker, or maybe just a piece of art with a lot of moving parts. Or maybe you want to drive a lot of LEDs with precise PWM output. Using only two pins, control 16 free-running PWM outputs! You can even chain up 62 breakouts to control up to 992 PWM outputs.
